# Fritzing sketch scheme (saved by Fritzing 0.9.3b)
breadboards: 1

parts:
  U1 = NodeMCU V1.0
  YwRobot_Power_Supply1 = YwRobot Breadboard Power Supply [part_number=545043]
  U4 = LCD-16X2 [package=lcd-16x2]
  LCM1602_IIC1 = LCM1602 IIC [part_number="LCM1602 IIC" chip_label="LCM1602 IIC" package="DIP (Dual Inline) [THT]"]
  ZS-042_RTC1 = ZS-042 RTC Module

nets:
  N1: U1.D1, LCM1602_IIC1.SCL, ZS-042_RTC1.SCL
  N2: U1.D2, LCM1602_IIC1.SDA, ZS-042_RTC1.SDA
  GND: U1.GND, YwRobot_Power_Supply1.GND#13, YwRobot_Power_Supply1.GND#14, LCM1602_IIC1.GND, ZS-042_RTC1.GND
  N3: YwRobot_Power_Supply1.VCC#5, YwRobot_Power_Supply1.VCC#6
  VCC: YwRobot_Power_Supply1.VCC#9, YwRobot_Power_Supply1.VCC#10, LCM1602_IIC1.VCC, ZS-042_RTC1.VCC
  N4: YwRobot_Power_Supply1.GND#11, YwRobot_Power_Supply1.GND#12
  VSS: U4.VSS, LCM1602_IIC1.VSS
  VDD: U4.VDD, LCM1602_IIC1.VDD
  N5: U4.VO, LCM1602_IIC1.V0
  N6: U4.RS, LCM1602_IIC1.RS
  N7: U4.R_W, LCM1602_IIC1.RW
  N8: U4.E, LCM1602_IIC1.E
  N9: U4.DB0, LCM1602_IIC1.D0
  N10: U4.DB1, LCM1602_IIC1.D1
  N11: U4.DB2, LCM1602_IIC1.D2
  N12: U4.DB3, LCM1602_IIC1.D3
  N13: U4.DB4, LCM1602_IIC1.D4
  N14: U4.DB5, LCM1602_IIC1.D5
  N15: U4.DB6, LCM1602_IIC1.D6
  N16: U4.DB7, LCM1602_IIC1.D7
  N17: U4.A, LCM1602_IIC1.A
  N18: U4.K, LCM1602_IIC1.K
  N19: LCM1602_IIC1.LED_A, LCM1602_IIC1.LED_B

custom parts:
  NodeMCU V1.0: ESP8266 based NodeMCU
  YwRobot Breadboard Power Supply: The YwRobot Breadboard Power Supply (MB-V2) has two power rails; they can be 5V or 3V3. Power to the module can be provided through the female USB socket or through the A10 (female) 2.1mm power jack.
  LCM1602 IIC: I2C-Module to use a 1602 or 2004 LCD on with the wire.h libory Serial LCD Modul
