# Fritzing sketch window_station (saved by Fritzing 0.9.3b)
breadboards: 1

parts:
  YwRobot_Power_Supply1 = YwRobot Breadboard Power Supply [part_number=545043]
  MOTOR1 = 28BYJ-48 Stepper Motor
  X1 = X113647 Stepper Driver Board [package=board]
  Part1 = Arduino Uno (Rev3) - ICSP

nets:
  N1: YwRobot_Power_Supply1.VCC#5, YwRobot_Power_Supply1.VCC#6
  N2: YwRobot_Power_Supply1.VCC#9, YwRobot_Power_Supply1.VCC#10, X1.+V
  N3: YwRobot_Power_Supply1.GND#11, YwRobot_Power_Supply1.GND#12
  GND: YwRobot_Power_Supply1.GND#13, YwRobot_Power_Supply1.GND#14, X1.GND, Part1.GND
  N4: MOTOR1.BLUE, X1.BLUE
  N5: MOTOR1.PINK, X1.PINK
  N6: MOTOR1.RED, X1.YELLOW
  N7: MOTOR1.ORANGE, X1.ORANGE
  N8: MOTOR1.YELLOW, X1.RED
  N9: X1.IN1, Part1.D8
  N10: X1.IN2, Part1.D9_PWM
  N11: X1.IN3, Part1.D10_PWM/SS
  N12: X1.IN4, Part1.D11_PWM/MOSI

custom parts:
  YwRobot Breadboard Power Supply: The YwRobot Breadboard Power Supply (MB-V2) has two power rails; they can be 5V or 3V3. Power to the module can be provided through the female USB socket or through the A10 (female) 2.1mm power jack.
  28BYJ-48 Stepper Motor: 28BYJ-48 gear-reduction stepper motor (small)
  X113647 Stepper Driver Board: A common stepper motor driver board based on ULN2003APG darlington array
